# Fritzing sketch ITER-8 (saved by Fritzing 1.0.0rc)
breadboards: 4

parts:
  Power_plug3 = USB-C plug
  S9 = Toggle Switch spst [package=THT]
  LED12 = LED - 5mm [color="Red (633nm)" current=20mA package="5 mm [THT]"]
  R35 = Resistor [tolerance=±5% power=0.25W resistance=150 package=THT]
  J5 = female pin header, 2 pins [form="♀ (female)"]
  R36 = Resistor [tolerance=±5% power=0.25W resistance=150 package=THT]  # not connected
  LED63 = LED - 5mm [color="Red (633nm)" current=20mA package="5 mm [THT]"]
  R37 = Resistor [tolerance=±5% power=0.25W resistance=1k package=THT]
  S10 = Momentary Switch [package=ksa_sealed_tac_switch]
  C40 = Ceramic Capacitor [capacitance=100nF voltage=35V package="200 mil [THT, multilayer]"]
  IC12 = IC, DIP package, 14 pins [chip_label=SN74HC00N]
  C41 = Ceramic Capacitor [capacitance=100nF voltage=35V package="200 mil [THT, multilayer]"]
  C42 = Ceramic Capacitor [capacitance=100nF voltage=35V package="200 mil [THT, multilayer]"]
  IC11 = IC, DIP package, 28 pins [chip_label=AT28C256-15PU]
  IC13 = IC, DIP package, 40 pins [chip_label=W65C22S6TPG-14]
  LCD1 = LCD screen
  VR3 = Trimpot-#3296-flat [part_number="10k Ohm" package=3386u]
  C43 = Ceramic Capacitor [capacitance=100nF voltage=35V package="200 mil [THT, multilayer]"]
  IC14 = IC, DIP package, 28 pins [chip_label=AS6C62256-55PCN]
  C44 = Ceramic Capacitor [capacitance=100nF voltage=35V package="200 mil [THT, multilayer]"]
  C45 = Ceramic Capacitor [capacitance=100nF voltage=35V package="200 mil [THT, multilayer]"]
  U14 = crystal oscillator tht [mpn=ECS-100AX-010]
  IC10 = IC, DIP package, 40 pins [chip_label=W65C02S6TPG-14]
  S11 = Momentary Switch [package=ksa_sealed_tac_switch]
  R38 = Resistor [tolerance=±5% power=0.25W resistance=1k package=THT]
  C46 = Electrolytic Capacitor [capacitance=100µF voltage=35V package="200 mil [THT, electrolytic]"]
  T1 = TMP36 Temperature Sensor [package="TO92 [THT]"]

nets:
  GND: Power_plug3.GND, R35.Pin_1, J5.pin1, S10.3, S10.4, C40.0, IC12.pin7, C41.0, C42.0, IC11.pin14, IC11.pin22, IC13.pin1, LCD1.VSS, LCD1.DB0, LCD1.DB1, LCD1.DB2, LCD1.DB3, LCD1.LED-, VR3.WIPER, C43.0, IC14.pin14, C44.0, C45.0, U14.Pin_7, IC10.pin21, S11.4, C46.-, T1.GND
  N1: Power_plug3.VCC, S9.COM, LED12.anode, J5.pin2
  N2: S9.L1, LED63.anode, R37.Pin_0, C40.1, IC12.pin4, IC12.pin5, IC12.pin14, C41.1, C42.1, IC11.pin27, IC11.pin28, IC13.pin20, LCD1.VDD, LCD1.LED+, C43.1, IC14.pin28, C44.1, C45.1, U14.Pin_14, IC10.pin2, IC10.pin6, IC10.pin8, IC10.pin36, IC10.pin38, R38.Pin_1, C46.+, T1.Vout
  N3: LED12.cathode, R35.Pin_0
  N4: R37.Pin_1, S10.1, S10.2, IC13.pin34, IC10.pin40, T1.+Vs
  N5: IC12.pin1, IC12.pin10, IC12.pin11, IC11.pin20
  N6: IC12.pin2, IC13.pin25, U14.Pin_8, IC10.pin37
  N7: IC12.pin3, IC14.pin20
  N8: IC12.pin8, IC13.pin23
  N9: IC12.pin9, IC11.pin1, IC14.pin1, IC14.pin22, IC10.pin24
  N10: IC12.pin12, IC12.pin13, IC10.pin25
  N11: IC11.pin2, IC14.pin2, IC10.pin22
  N12: IC11.pin3, IC14.pin3, IC10.pin16
  N13: IC11.pin4, IC14.pin4, IC10.pin15
  N14: IC11.pin5, IC14.pin5, IC10.pin14
  N15: IC11.pin6, IC14.pin6, IC10.pin13
  N16: IC11.pin7, IC13.pin35, IC14.pin7, IC10.pin12
  N17: IC11.pin8, IC13.pin36, IC14.pin8, IC10.pin11
  N18: IC11.pin9, IC13.pin37, IC14.pin9, IC10.pin10
  N19: IC11.pin10, IC13.pin38, IC14.pin10, IC10.pin9
  N20: IC11.pin11, IC13.pin33, IC14.pin11, IC10.pin33
  N21: IC11.pin12, IC13.pin32, IC14.pin12, IC10.pin32
  N22: IC11.pin13, IC13.pin31, IC14.pin13, IC10.pin31
  N23: IC11.pin15, IC13.pin30, IC14.pin15, IC10.pin30
  N24: IC11.pin16, IC13.pin29, IC14.pin16, IC10.pin29
  N25: IC11.pin17, IC13.pin28, IC14.pin17, IC10.pin28
  N26: IC11.pin18, IC13.pin27, IC14.pin18, IC10.pin27
  N27: IC11.pin19, IC13.pin26, IC14.pin19, IC10.pin26
  N28: IC11.pin21, IC14.pin21, IC10.pin19
  N29: IC11.pin23, IC14.pin23, IC10.pin20
  N30: IC11.pin24, IC14.pin24, IC10.pin18
  N31: IC11.pin25, IC14.pin25, IC10.pin17
  N32: IC11.pin26, IC13.pin24, IC14.pin26, IC10.pin23
  N33: IC13.pin11, LCD1.RS
  N34: IC13.pin12, LCD1.R/W
  N35: IC13.pin13, LCD1.E
  N36: IC13.pin14, LCD1.DB4
  N37: IC13.pin15, LCD1.DB5
  N38: IC13.pin16, LCD1.DB6
  N39: IC13.pin17, LCD1.DB7
  N40: IC13.pin21, IC10.pin4
  N41: IC13.pin22, IC14.pin27, IC10.pin34
  N42: IC13.pin40, S11.1
  N43: LCD1.V0, VR3.CW
  N44: S11.2, R38.Pin_0

notes:
  Wire colors
  Red - VCC
  Black - GND
  Blue - Data
  Green - Address
  White - Clock
  Yellow - Operation control
  Brown - Generic
  Grey - Component
  Pink - Temporary

custom parts:
  USB-C plug: power plug
  Toggle Switch spst: Toggle Switch single pole single throw
  Trimpot-#3296-flat: Bourns #3296 Square Trimpot 25 turn lying flat for low profile
  crystal oscillator tht: Generic crystal oscillator tht.
