# Fritzing sketch Debugger (saved by Fritzing 1.0.4)
breadboards: 1

parts:
  Part1 = Arduino Mega 2560 (Rev3)
  J20 = female pin header, 8 pins [form="♀ (female)"]
  J21 = female pin header, 8 pins [form="♀ (female)"]
  J23 = female pin header, 4 pins [form="♀ (female)"]
  J24 = female pin header, 4 pins [form="♀ (female)"]
  Connector_6 = female pin header, 1 pin [form="♀ (female)"]
  Connector_7 = female pin header, 1 pin [form="♀ (female)"]
  J25 = female pin header, 8 pins [form="♀ (female)"]
  J27 = female pin header, 8 pins [form="♀ (female)"]
  J28 = female pin header, 4 pins [form="♀ (female)"]
  J29 = female pin header, 4 pins [form="♀ (female)"]
  Connector_8 = female pin header, 1 pin [form="♀ (female)"]
  Connector_9 = female pin header, 1 pin [form="♀ (female)"]
  Connector_10 = female pin header, 1 pin [form="♀ (female)"]
  Connector_11 = female pin header, 1 pin [form="♀ (female)"]
  J30 = female pin header, 8 pins [form="♀ (female)"]
  J31 = Power Jack [package=power_jack_slot]
  J34 = female pin header, 2 pins [form="♀ (female)"]
  S19 = Momentary Switch [package=ksa_sealed_tac_switch]
  S20 = Toggle Switch [package=THT]
  R58 = Resistor [tolerance=±5% power=0.25W resistance=1k package=THT]
  Connector_14 = female pin header, 1 pin [form="♀ (female)"]
  J35 = female pin header, 1 pin [form="♀ (female)"]
  R59 = Resistor [tolerance=±5% power=0.25W resistance=1k package=THT]
  J36 = female pin header, 1 pin [form="♀ (female)"]
  J37 = female pin header, 1 pin [form="♀ (female)"]

nets:
  N1: Part1.D2_PWM, Connector_7.pin1, Connector_8.pin1
  N2: Part1.D3_PWM, Connector_6.pin1, Connector_9.pin1
  N3: Part1.D4_PWM, Connector_10.pin1
  N4: Part1.D5_PWM, Connector_11.pin1
  N5: Part1.D22, J20.pin8, J27.pin8
  N6: Part1.D23, J30.pin8
  N7: Part1.D24, J20.pin7, J27.pin7
  N8: Part1.D25, J30.pin7
  N9: Part1.D26, J20.pin6, J27.pin6
  N10: Part1.D27, J30.pin6
  N11: Part1.D28, J20.pin5, J27.pin5
  N12: Part1.D29, J30.pin5
  N13: Part1.D30, J20.pin4, J27.pin4
  N14: Part1.D31, J30.pin4
  N15: Part1.D32, J20.pin3, J27.pin3
  N16: Part1.D33, J30.pin3
  N17: Part1.D34, J20.pin2, J27.pin2
  N18: Part1.D35, J30.pin2
  N19: Part1.D36, J20.pin1, J27.pin1
  N20: Part1.D37, J30.pin1
  N21: Part1.D38, J23.pin4, J28.pin4
  N22: Part1.D39, J21.pin8, J25.pin8
  N23: Part1.D40, J23.pin3, J28.pin3
  N24: Part1.D41, J21.pin7, J25.pin7
  N25: Part1.D42, J23.pin2, J28.pin2
  N26: Part1.D43, J21.pin6, J25.pin6
  N27: Part1.D44, J23.pin1, J28.pin1
  N28: Part1.D45, J21.pin5, J25.pin5
  N29: Part1.D46, J24.pin4, J29.pin4
  N30: Part1.D47, J21.pin4, J25.pin4
  N31: Part1.D48, J24.pin3, J29.pin3
  N32: Part1.D49, J21.pin3, J25.pin3
  N33: Part1.D50, J24.pin2, J29.pin2
  N34: Part1.D51, J21.pin2, J25.pin2
  N35: Part1.D52, J24.pin1, J29.pin1
  N36: Part1.D53, J21.pin1, J25.pin1
  N37: J31.GND, J34.pin1, S19.3, R58.Pin_1
  N38: J31.PWR, J34.pin2, S20.COM, R59.Pin_1
  N39: S19.1, R59.Pin_0, J36.pin1, J37.pin1
  N40: S20.L1, R58.Pin_0, Connector_14.pin1, J35.pin1

notes:
  Wire colors
  Red - VCC
  Black - GND
  White - Clock
  Yellow - Operation control
  Clock
  R/W
  Select
  Resume / Step
  Address
  Data 1
  Data 2
