# Fritzing sketch Debugger_breadboard (saved by Fritzing 1.0.4)
breadboards: 1

parts:
  IC18 = IC, DIP package, 14 pins [chip_label=SN74LS04N]
  IC19 = IC, DIP package, 14 pins [chip_label=SN74LS08N]
  IC20 = IC, DIP package, 14 pins [chip_label=SN74LS32N]
  J16 = female pin header, 1 pin [form="♀ (female)"]
  J17 = female pin header, 1 pin [form="♀ (female)"]
  J18 = female pin header, 2 pins [form="♀ (female)"]
  U18 = 555 Timer [package="DIP8 [THT]"]
  LED67 = LED - 5mm [color="White (8000K)" current=20mA package="5 mm [THT]"]
  R50 = Resistor [tolerance=±5% power=0.25W resistance=100 package=THT]
  R51 = Resistor [tolerance=±5% power=0.25W resistance=1k package=THT]
  VR5 = Trimpot-#3296-flat [part_number="1M Ohm" package=3386u]
  C64 = Ceramic Capacitor [capacitance=10nF voltage=35V package="200 mil [THT, multilayer]"]
  R52 = Resistor [tolerance=±5% power=0.25W resistance=1k package=THT]
  LED68 = LED - 5mm [color="White (8000K)" current=20mA package="5 mm [THT]"]
  U19 = 555 Timer [package="DIP8 [THT]"]
  S17 = Momentary Switch [package=ksa_sealed_tac_switch]
  C65 = Ceramic Capacitor [capacitance=1µF voltage=35V package="100 mil [THT, multilayer]"]
  C66 = Ceramic Capacitor [capacitance=100nF voltage=35V package="200 mil [THT, multilayer]"]
  C67 = Ceramic Capacitor [capacitance=100nF voltage=35V package="200 mil [THT, multilayer]"]
  C68 = Ceramic Capacitor [capacitance=100nF voltage=35V package="200 mil [THT, multilayer]"]
  C69 = Ceramic Capacitor [capacitance=100nF voltage=35V package="200 mil [THT, multilayer]"]
  C70 = Ceramic Capacitor [capacitance=100nF voltage=35V package="200 mil [THT, multilayer]"]
  C71 = Ceramic Capacitor [capacitance=100nF voltage=35V package="200 mil [THT, multilayer]"]
  R53 = Resistor [tolerance=±5% power=0.25W resistance=1M package=THT]
  C72 = Ceramic Capacitor [capacitance=100nF voltage=35V package="200 mil [THT, multilayer]"]
  C73 = Ceramic Capacitor [capacitance=10nF voltage=35V package="200 mil [THT, multilayer]"]
  LED69 = LED - 5mm [color="White (8000K)" current=20mA package="5 mm [THT]"]
  R54 = Resistor [tolerance=±5% power=0.25W resistance=100 package=THT]
  U20 = 555 Timer [package="DIP8 [THT]"]
  S18 = Toggle Switch [package=THT]
  C74 = Ceramic Capacitor [capacitance=10nF voltage=35V package="200 mil [THT, multilayer]"]
  R55 = Resistor [tolerance=±5% power=0.25W resistance=1k package=THT]
  R56 = Resistor [tolerance=±5% power=0.25W resistance=1k package=THT]
  R57 = Resistor [tolerance=±5% power=0.25W resistance=1k package=THT]
  J19 = Power Jack [package=power_jack_slot]
  Connector_3 = female pin header, 1 pin [form="♀ (female)"]
  Connector_5 = female pin header, 1 pin [form="♀ (female)"]
  Part1 = Arduino Mega 2560 (Rev3)
  J20 = female pin header, 8 pins [form="♀ (female)"]
  J21 = female pin header, 8 pins [form="♀ (female)"]
  J23 = female pin header, 4 pins [form="♀ (female)"]
  J24 = female pin header, 4 pins [form="♀ (female)"]
  Connector_6 = female pin header, 1 pin [form="♀ (female)"]
  Connector_7 = female pin header, 1 pin [form="♀ (female)"]
  J25 = female pin header, 8 pins [form="♀ (female)"]
  J27 = female pin header, 8 pins [form="♀ (female)"]
  J28 = female pin header, 4 pins [form="♀ (female)"]
  J29 = female pin header, 4 pins [form="♀ (female)"]
  Connector_8 = female pin header, 1 pin [form="♀ (female)"]
  Connector_9 = female pin header, 1 pin [form="♀ (female)"]
  Connector_10 = female pin header, 1 pin [form="♀ (female)"]
  Connector_11 = female pin header, 1 pin [form="♀ (female)"]
  Connector_12 = female pin header, 1 pin [form="♀ (female)"]
  Connector_13 = female pin header, 1 pin [form="♀ (female)"]
  J30 = female pin header, 8 pins [form="♀ (female)"]

nets:
  N1: IC18.pin1, IC19.pin2, U20.Output
  N2: IC18.pin2, IC19.pin9
  N3: IC18.pin3, IC18.pin7, IC19.pin7, IC20.pin7, J17.pin1, J18.pin1, U18.Ground, LED67.cathode, R50.Pin_1, C64.0, U19.Ground, S17.3, C65.1, C66.0, C67.0, C68.0, C69.0, C70.0, C71.0, C72.1, C73.1, R54.Pin_0, U20.Ground, U20.Threshold, S18.COM, C74.0, J19.GND, Connector_5.pin1
  N4: IC18.pin4, IC19.pin12
  N5: IC18.pin5, IC18.pin9, IC18.pin11, IC18.pin13, IC18.pin14, IC19.pin4, IC19.pin5, IC19.pin14, IC20.pin1, IC20.pin2, IC20.pin4, IC20.pin5, IC20.pin12, IC20.pin13, IC20.pin14, J18.pin2, U18.Reset, U18.Vcc_Supply_Voltage, R51.Pin_1, U19.Reset, U19.Vcc_Supply_Voltage, C66.1, C67.1, C68.1, C69.1, C70.1, C71.1, R53.Pin_1, U20.Vcc_Supply_Voltage, R55.Pin_1, R56.Pin_1, R57.Pin_1, J19.PWR
  N6: IC19.pin1, U18.Output, LED68.anode
  N7: IC19.pin3, IC20.pin9
  N8: IC19.pin8, IC20.pin10
  N9: IC19.pin10, U19.Output, LED69.anode
  N10: IC19.pin11, J16.pin1, LED67.anode, Connector_3.pin1
  N11: IC19.pin13, IC20.pin8
  N12: U18.Trigger, U18.Threshold, VR5.CCW, C65.0
  N13: U18.Control_Voltage, C64.1
  N14: U18.Discharge, R51.Pin_0, R52.Pin_0
  N15: R50.Pin_0, LED68.cathode
  N16: VR5.WIPER, R52.Pin_1
  N17: U19.Trigger, S17.1, R57.Pin_0, Connector_12.pin1, Connector_13.pin1
  N18: U19.Control_Voltage, C73.0
  N19: U19.Threshold, U19.Discharge, R53.Pin_0, C72.0
  N20: LED69.cathode, R54.Pin_1
  N21: U20.Trigger, S18.L1, R55.Pin_0
  N22: U20.Reset, S18.L2, R56.Pin_0
  N23: U20.Control_Voltage, C74.1
  N24: Part1.D18/TX1, Connector_10.pin1
  N25: Part1.D2_PWM, Connector_7.pin1, Connector_8.pin1
  N26: Part1.D3_PWM, Connector_6.pin1, Connector_9.pin1
  N27: Part1.D4_PWM, Connector_11.pin1
  N28: Part1.D22, J20.pin8, J27.pin8
  N29: Part1.D23, J30.pin8
  N30: Part1.D24, J20.pin7, J27.pin7
  N31: Part1.D25, J30.pin7
  N32: Part1.D26, J20.pin6, J27.pin6
  N33: Part1.D27, J30.pin6
  N34: Part1.D28, J20.pin5, J27.pin5
  N35: Part1.D29, J30.pin5
  N36: Part1.D30, J20.pin4, J27.pin4
  N37: Part1.D31, J30.pin4
  N38: Part1.D32, J20.pin3, J27.pin3
  N39: Part1.D33, J30.pin3
  N40: Part1.D34, J20.pin2, J27.pin2
  N41: Part1.D35, J30.pin2
  N42: Part1.D36, J20.pin1, J27.pin1
  N43: Part1.D37, J30.pin1
  N44: Part1.D38, J23.pin4, J28.pin4
  N45: Part1.D39, J21.pin8, J25.pin8
  N46: Part1.D40, J23.pin3, J28.pin3
  N47: Part1.D41, J21.pin7, J25.pin7
  N48: Part1.D42, J23.pin2, J28.pin2
  N49: Part1.D43, J21.pin6, J25.pin6
  N50: Part1.D44, J23.pin1, J28.pin1
  N51: Part1.D45, J21.pin5, J25.pin5
  N52: Part1.D46, J24.pin4, J29.pin4
  N53: Part1.D47, J21.pin4, J25.pin4
  N54: Part1.D48, J24.pin3, J29.pin3
  N55: Part1.D49, J21.pin3, J25.pin3
  N56: Part1.D50, J24.pin2, J29.pin2
  N57: Part1.D51, J21.pin2, J25.pin2
  N58: Part1.D52, J24.pin1, J29.pin1
  N59: Part1.D53, J21.pin1, J25.pin1

notes:
  Wire colors
  Red - VCC
  Black - GND
  White - Clock
  Yellow - Operation control
  Brown - Generic
  5V
  Clock
  Halt
  R/W
  Resume
  Address
  Data 1
  Data 2

custom parts:
  Trimpot-#3296-flat: Bourns #3296 Square Trimpot 25 turn lying flat for low profile
